# Fritzing sketch ygrasia (saved by Fritzing 0.9.6b)
breadboards: 1

parts:
  Εξάρτημα1 = Arduino Uno (Rev3)
  Εξάρτημα2 = Soil Moisture Sensor
  Εξάρτημα3 = Soil Moisture Sensor

nets:
  N1: Εξάρτημα1.A0, Εξάρτημα3.SIG
  N2: Εξάρτημα1.A1, Εξάρτημα2.SIG
  VCC: Εξάρτημα1.5V, Εξάρτημα2.VCC, Εξάρτημα3.VCC
  GND: Εξάρτημα1.GND, Εξάρτημα2.GND, Εξάρτημα3.GND
